# Fritzing sketch wallpad_bridge_wtAMS1117 (saved by Fritzing 1.0.6)
circuit board: 6.74875cm x 5.00722cm
stripboards: 3

parts:
  WeMos_D1_Mini1 = WeMos D1 Mini
  U1 = V_REG_LD1117VXX [package=78xxl]
  Component2 = RS485_XY-017_mir [part_number=XY-017]
  U2 = Sharp PC817 [package=THT]
  U3 = Sharp PC817 [package=THT]
  R2 = Resistor [tolerance=±5% power=0.25W resistance=1k package=THT]
  R3 = Resistor [tolerance=±5% power=0.25W resistance=1k package=THT]
  J4 = molex pin header, 3 pins [form=molex]
  J2 = molex pin header, 5 pins [form=molex]

nets:
  3V3: WeMos_D1_Mini1.3V3, Component2.VCC
  N1: WeMos_D1_Mini1.5V, U1.OUT
  N2: WeMos_D1_Mini1.D1, Component2.TXD
  N3: WeMos_D1_Mini1.D2, Component2.RXD
  N4: WeMos_D1_Mini1.D5, U3.Pin_4
  N5: WeMos_D1_Mini1.D6, U2.Pin_4
  GND: WeMos_D1_Mini1.G, U1.GND, Component2.GND, U2.Pin_2, U2.Pin_3, U3.Pin_2, U3.Pin_3, J4.pin1
  N6: U1.IN, J4.pin3
  N7: Component2.A, J2.pin1
  N8: Component2.B, J2.pin2
  N9: U2.Pin_1, R3.Pin_1
  N10: U3.Pin_1, R2.Pin_1
  N11: R2.Pin_0, J2.pin5
  N12: R3.Pin_0, J2.pin4

notes:
  [1] [2] [3] [4] [5]
  RX TX - Mt. spr.
  [1] RX
  [2] TX
  [3] GND
  [4] 12V
  [1] [2] [3]
  0V - 12V

custom parts:
  RS485_XY-017_mir: Commercially available RS485 to RS232 TTL Module
